# Fritzing sketch 02_pushButton+LED (saved by Fritzing 0.7.7b)
breadboards: 1

parts:
  Arduino1 = Arduino
  LED1 = LED - 5mm [color="Red (633nm)" package="5 mm [THT]"]
  R1 = Resistor [tolerance=±5% resistance=220 package=THT]
  S1 = Pushbutton [package="[THT]"]
  R2 = Resistor [tolerance=±5% resistance=220 package=THT]

nets (from the breadboard view):
  N1: Arduino1.GND, LED1.cathode, R2.Pin_0
  N2: Arduino1.D11, R1.Pin_0
  N3: Arduino1.D2, S1.Pin_1, S1.Pin_2, R2.Pin_1
  N4: Arduino1.+5V, S1.Pin_3, S1.Pin_4
  N5: LED1.anode, R1.Pin_1
