# Fritzing sketch analogRW (saved by Fritzing 0.7.5b)
breadboards: 1

parts:
  Arduino1 = Arduino
  LED1 = LED - 5mm [color="Red (633nm)" package="5 mm [THT]"]
  R1 = Resistor [tolerance=±5% resistance=220 package=THT]
  R3 = Rotary Potentiometer (Small) [maximum_resistance=100kΩ]
  R4 = Resistor [tolerance=±5% resistance=100 package=THT]
  R5 = Slide Potentiometer [maximum_resistance=100kΩ]
  R7 = Resistor [tolerance=±5% resistance=100 package=THT]
  Arduino2 = Arduino
  R8 = Resistor [tolerance=±5% resistance=220 package=THT]
  LED2 = LED - 5mm [color="Red (633nm)" package="5 mm [THT]"]

nets:
  GND: Arduino1.GND, LED1.cathode, R3.leg1, R5.leg1, Arduino2.GND, LED2.cathode
  N1: Arduino1.D11, R1.Pin_0
  5V: Arduino1.+5V, R4.Pin_0, R7.Pin_0, Arduino2.+5V
  N2: Arduino1.A0, R3.wiper
  N3: LED1.anode, R1.Pin_1
  N4: R3.leg2, R4.Pin_1
  N5: R5.wiper, Arduino2.A0
  N6: R5.leg2, R7.Pin_1
  N7: Arduino2.D11, R8.Pin_0
  N8: R8.Pin_1, LED2.anode
