# Fritzing sketch piezoTone (saved by Fritzing 0.7.5b)
breadboards: 1

parts:
  Arduino1 = Arduino
  R1 = Resistor [tolerance=±5% resistance=100 package=THT]
  R4 = Resistor [tolerance=±5% resistance=1k package=THT]
  R5 = Photocell (LDR) [package=THT]
  J1 = Piezo Speaker

nets (from the breadboard view):
  N1: Arduino1.GND, R1.Pin_1, R4.Pin_1
  N2: Arduino1.D11, J1.pin2
  N3: Arduino1.+5V, R5.pin_0
  N4: Arduino1.A0, R4.Pin_0, R5.pin_1
  N5: R1.Pin_0, J1.pin1
